# Fritzing sketch LPD_Circuit Diagram (saved by Fritzing 0.9.5d)
# 18650 Li-ion Battery: CC-BY Dr Kristofer Chan, King's College London/Remote-research.org
breadboards: 1

parts:
  esp1 = ESP32 DevKitc V4
  Part1 = Soil Moisture Sensor
  DHT1 = DHT11 Humitidy and Temperature Sensor (3 pins)
  DS1 = DS18B20 1-Wire Temperature Sensor [part_number=DS18B20]
  Part2 = LCD1602-I2C
  BAT1 = 18650 Li-ion Battery [package=battery-18650]
  MOD1 = MT3608 Boost No usb
  TP1 = TP4056 [chip_label=TP4056 package="DIP (Dual Inline) [THT]"]
  R1 = Resistor [tolerance=±5% resistance=4.7k package="0805 [SMD]"]

nets:
  N1: esp1.IO4, DHT1.Signal
  N2: esp1.IO21, Part2.SDA
  N3: esp1.IO22, Part2.SCL
  GND: esp1.GND#18, DHT1.Gnd, Part2.GND, MOD1.IN_(-), MOD1.OUT_(-), TP1.pin6
  3V3: esp1.3V3, Part2.VCC
  N4: esp1.IO34, Part1.SIG
  N5: esp1.IO25, DS1.DQ, R1.Pin_0
  N6: esp1.5V, MOD1.OUT_(+)
  GND_2: Part1.GND, DS1.GND
  N7: Part1.VCC, DHT1.Plus
  N8: DS1.VDD, R1.Pin_1
  N9: BAT1.-, TP1.pin5
  N10: BAT1.+, TP1.pin4
  N11: MOD1.IN_(+), TP1.pin3

notes:
  RED WIRE - POWER (VCC)
  BLACK WIRE - GROUND
  YELLOW WIRE - DATAPIN
  DHT11
  Soil Moisture Sensor
  Soil Temperature Sesnor
  Power Source

custom parts:
  ESP32 DevKitc V4: ESP32-DevKitC board with ESP32-WROOM-32 module. ESP32-DevKitC V4 is a small-sized ESP32-based development board produced by Espressif. Most of the pins on the ESP module are broken out to the pin headers on the board. The pins D0, D1, D2, D3, CMD and CLK are used internally for communication between ESP32 and SPI flash memory. They are grouped on both sides near the USB connector. Avoid using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
  DHT11 Humitidy and Temperature Sensor (3 pins): DHT11 Humidity and Temperature Sensor (3 pins).
  LCD1602-I2C: A standard character display, usually with 2x16 characters. Comes in many colors with LCM1602 IIC attached.
  18650 Li-ion Battery: 18650 li-ion Battery Standard 18650 battery with interactive connectors Creative Common Attribution 4.0 International (CC-BY 4.0) license. Any use of this part requires attribution of Dr Kristofer Chan, Department of Geography, King's College London. Contact kristofer.chan [at] kcl.ac.uk OR kris [at] remote-research.org for further information.
  MT3608 Boost No usb: Chip- MT3608 / B6289 DC to DC step up, power booster module. With adjustable output voltage. Current- 2A . || Input voltage- 2V-24V || Output voltage- 5V-28V Input interface- Inversed polarity- NO. || Led indicator- No.
  TP4056: A DIP stand-in part for whatever IC you want. With 6 pins on a 300mil dual inline package (DIP) footprint.
